# Fritzing sketch birdhouse (saved by Fritzing 0.9.3b)
breadboards: 2

parts:
  Part1 = Photon
  LED1 = smd LED [color="Green (570nm)" package="0805 [SMD]"]
  LED2 = smd LED [color="Red (633nm)" package="0603 [SMD]"]
  LED3 = smd LED [color="Yellow (592nm)" package="0603 [SMD]"]
  HC-SR04_Sensor_1 = HC-SR04 Ultrasonic Distance Sensor
  R4 = Resistor [tolerance=±5% resistance=10 package=THT]  # not connected
  S1 = Pushbutton [package="[SMD]"]
  R5 = Resistor [tolerance=±5% resistance=10 package=THT]
  R6 = Resistor [tolerance=±5% resistance=10 package=THT]
  R7 = Resistor [tolerance=±5% resistance=10 package=THT]

nets:
  GND: Part1.GND, HC-SR04_Sensor_1.GND, R5.Pin_0, R6.Pin_0, R7.Pin_0
  VIN: Part1.VIN, HC-SR04_Sensor_1.VCC, S1.Pin_3, S1.Pin_4
  N1: Part1.D0, LED1.anode
  N2: Part1.D1, LED3.anode
  N3: Part1.D2, HC-SR04_Sensor_1.ECHO
  N4: Part1.D3, HC-SR04_Sensor_1.TRIG
  N5: Part1.D4, S1.Pin_1, S1.Pin_2, R7.Pin_1
  N6: Part1.D5, LED2.anode
  N7: LED1.cathode, R6.Pin_1
  N8: LED2.cathode, R5.Pin_1
